# Fritzing sketch ProyectoIoT (saved by Fritzing 0.9.8b)
breadboards: 1

parts:
  Raspberry_Pi_1 = Raspberry Pi 3 [part_number=RPI-3-V1.2]
  DHT11 = Humidity and Temperature Sensor RHT03
  MQ-7 = GAS_SENSOR [package=mq-3]
  MQ-4 = GAS_SENSOR [package=mq-3]
  R1 = Resistor [tolerance=±5% power=0.25 resistance=10k package=THT]

nets:
  3V3: Raspberry_Pi_1.3v3, Raspberry_Pi_1.3V3, DHT11.Vcc, MQ-7.B1, MQ-4.B1, R1.Pin_0
  N1: Raspberry_Pi_1.GPIO23, DHT11.Data-signal, R1.Pin_1
  N2: Raspberry_Pi_1.GND, DHT11.GND_1, MQ-7.A1, MQ-4.A1
  N3: MQ-7.H1, MQ-7.H2, MQ-4.H1, MQ-4.H2
